# Fritzing sketch krets (saved by Fritzing 0.9.3b)
breadboards: 1

parts:
  Part1 = Arduino Mega 2560 (Rev3)
  Part3 = Adafruit INA219 [part_number="Adafruit #904"]
  A1 = AS5600 module
  M1 = DC Motor
  JACK1 = 2.1mm Barrel Jack with Terminal Block

nets:
  N1: Part1.D21/SCL, Part3.SCL, A1.Pin_6
  N2: Part1.D20/SDA, Part3.SDA, A1.Pin_5
  3V3: Part1.3V3, Part3.VCC, A1.Pin_1
  GND: Part1.GND, Part3.GND, A1.Pin_3
  N3: Part3.VIN-, M1.pin_2
  N4: Part3.VIN+, JACK1.POS
  N5: M1.pin_1, JACK1.NEG

custom parts:
  Adafruit INA219: This breakout board will solve all your power-monitoring problems. Instead of struggling with two multimeters, you can just use the handy INA219B chip on this breakout to both measure both the high side voltage and DC current draw over I2C with 1% precision. Most current-measuring devices such as our current panel meter are only good for low side measuring. That means that unless you want to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
  AS5600 module: .This module is mainly placed behind the stepper motor to obtain the rotation angle of the stepper motor.
